# Fritzing sketch cleaner-robot-electronic-schema (saved by Fritzing 0.9.3b)
breadboards: 1

parts:
  U3 = ESP 32 DEVKIT DOIT
  L298N2 = L298N DC motor driver
  VCC1 = Battery block 9V
  Right_Motors = DC Motor
  Left_Motors = DC Motor
  right-sensor = HC-SR04 Ultrasonic Distance Sensor
  front-sensor = HC-SR04 Ultrasonic Distance Sensor
  left-sensor = HC-SR04 Ultrasonic Distance Sensor

nets:
  N1: U3.D23, L298N2.IN3
  N2: U3.D22, U3.D18, U3.3V3, L298N2.IN2, L298N2.IN4
  N3: U3.D19, L298N2.IN1
  N4: U3.D13, U3.D14, L298N2.ENB, right-sensor.ECHO
  N5: U3.D12, right-sensor.TRIG
  N6: U3.D26, front-sensor.ECHO
  N7: U3.D25, front-sensor.TRIG
  N8: U3.D33, left-sensor.TRIG
  N9: U3.D32, left-sensor.ECHO, left-sensor.GND
  N10: L298N2.OUT1, Left_Motors.pin_1
  N11: L298N2.OUT2, Left_Motors.pin_2
  N12: L298N2.OUT3, Right_Motors.pin_2
  N13: L298N2.OUT4, Right_Motors.pin_1
  N14: L298N2.12V, VCC1.+
  N15: L298N2.GND, VCC1.-

custom parts:
  L298N DC motor driver: 2x DC motor driver with 78M05 positive voltage regulator (7..35 V) L298N: max 46 V, 2 A Set 5 V Enable jumper to enable 5 V regultor (needed for the L298N) and +5 V output at screw terminal or supply external +5 V at screw terminal Set ENA and/or ENB to +5 V to enable motor permanently or supply ENA and/or ENB with PWM signal IN1 and IN2 set rotation directory for motor A (OUT1/OUT2) IN2 and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
